# Fritzing sketch Nerf-Target (saved by Fritzing 0.9.9b)

parts:
  Arduino = Arduino Uno (Rev3)
  Servo = Basic Servo
  LED1 = LED - 5mm [color="Red (633nm)" current=0.030 package="5 mm [THT]"]
  R1 = Resistor [tolerance=±5% resistance=220 package="0402 [SMD]"]
  Trigger = Pushbutton [package=THT]
  R2 = Resistor [tolerance=±5% resistance=150 package="0402 [SMD]"]

nets:
  N1: Arduino.D8, Trigger.leg0, R2.Pin_1
  N2: Arduino.D13/SCK, R1.Pin_0
  GND: Arduino.GND, Servo.gnd, LED1.cathode, Trigger.leg1
  N3: Arduino.D3_PWM, Servo.pulse
  N4: Arduino.3V3, R2.Pin_0
  5V: Arduino.5V, Servo.vcc
  N5: LED1.anode, R1.Pin_1
